# Fritzing sketch MFRC522 (saved by Fritzing 0.9.3b)

parts:
  Part6 = Arduino Uno (Rev3)
  Part7 = RFID-RC522-v3
  Part8 = RFID-RC522-v3
  Part9 = RFID-RC522-v3
  Part10 = RFID-RC522-v3
  Part12 = Adafruit 4-channel I2C-safe Bi-directional Logic Level Converter [part_number="Adafruit #757"]
  Part13 = Adafruit 4-channel I2C-safe Bi-directional Logic Level Converter [part_number="Adafruit #757"]
  KY-2 = Keyes Relay [package=THT]
  JACK3 = 2.1mm Barrel Jack with Terminal Block
  L2 = MagLock
  JACK4 = 2.1mm Barrel Jack with Terminal Block
  JACK5 = 2.1mm Barrel Jack with Terminal Block

nets:
  N1: Part6.A0, KY-2.signal
  N2: Part6.D8, Part12.B1
  N3: Part6.D11_PWM/MOSI, Part12.B2
  N4: Part6.D12/MISO, Part12.B3
  N5: Part6.D13/SCK, Part12.B4
  GND: Part6.GND, Part7.IRQ, Part7.GND, Part8.GND, Part9.IRQ, Part9.GND, Part10.GND, Part12.GND, Part13.GND, KY-2.ground, JACK4.NEG, JACK5.NEG
  N6: Part6.D2, Part13.B1
  N7: Part6.D3_PWM, Part13.B2
  N8: Part6.D4, Part13.B3
  N9: Part6.D5_PWM, Part13.B4
  N10: Part6.5V, Part12.HV, Part13.HV, KY-2.power, JACK5.POS
  N11: Part7.SDA, Part13.A2
  N12: Part7.SCK, Part8.SCK, Part9.SCK, Part10.SCK, Part12.A4
  N13: Part7.MOSI, Part8.MOSI, Part9.MOSI, Part10.MOSI, Part12.A2
  N14: Part7.MISO, Part8.MISO, Part9.MISO, Part10.MISO, Part12.A3
  N15: Part7.RST, Part8.RST, Part9.RST, Part10.RST, Part12.A1
  3.3V: Part7.3.3V, Part8.3.3V, Part9.3.3V, Part10.3.3V, Part12.LV, Part13.LV, JACK4.POS
  N16: Part8.SDA, Part13.A3
  N17: Part9.SDA, Part13.A1
  N18: Part10.SDA, Part13.A4
  N19: KY-2.C, KY-2.NO, JACK3.POS, L2.pin2
  N20: JACK3.NEG, L2.pin1

notes:
  All the readers share the same SPI signal wires (MOSI, MISO, and SCK). They also share a single RESET line.
  These are all routed through the left-hand side logic level shifter, to convert between 3.3V logic on the low reader side and 5V on the high Arduino side.
  Arduino (Hi)Shifter(Lo) RFID Readers Wire Colour
  Pin 8 A1 B1 RESET Brown
  Pin 11 A2 B2 MOSI Blue
  Pin 12 A3 B3 MISO Purple
  Pin 13 A4 B4 SCK Green
  Pin 5V HV Red
  Pin 3.3V LV Orange
  GND GND GND Black
  Each reader has a unique NSS line (yellow), which is pulled low by the Arduino to specify which device is being communicated with.
  These lines are all assigned a unique GPIO pin on the Arduino which is then routed through the high side of the right-hand side logic level shifter, then from the low side of the reader to the NSS pin.
  Arduino (Hi)Shifter(Lo) RFID Reader
  Pin 2 A1 B1 Reader#1 NSS
  Pin 3 A2 B2 Reader#2 NSS
  Pin 4 A3 B3 Reader#3 NSS
  Pin 5 A4 B4 Reader#4 NSS
  5V HV
  3.3V LV
  GND GND GND
  3.3V DC (for RFID readers)
  5V DC (for Arduino and Relay)
  12V DC (for Maglock)

custom parts:
  RFID-RC522-v3: A simple China made RFID-RC522 Reader (6x4 cm); do check the pin labels, as this is a MFRC522 based clone.
  Adafruit 4-channel I2C-safe Bi-directional Logic Level Converter: Because the Arduino (and Basic Stamp) are 5V devices, and most modern sensors, displays, flash cards and modes are 3.3V-only, many makers find that they need to perform level shifting/conversion to protect the 3.3V device from 5V. We do have some other handy level shifters in the shop, from the DIP 74LVC245 to the fancy bi-directional TXB0108. However, neither of these are happy to work with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
  Keyes Relay: The Keyes 5V relay module is suitable for SCM development, home appliance control. It uses a 5V~12V TIL control signal which can control DC / AC signal.
