# Fritzing sketch Mega RFID (saved by Fritzing 0.9.4)
breadboards: 1

parts:
  Part2 = RFID-RC522-v3
  Part3 = RFID-RC522-v3
  KY-1 = Keyes Relay [package=THT]
  JACK1 = 2.1mm Barrel Jack with Terminal Block
  L1 = MagLock
  Part5 = RFID-RC522-v3
  Part15 = Arduino Uno (Rev3)
  R1 = Resistor [tolerance=±5% resistance=10k package=THT]
  R2 = Resistor [tolerance=±5% resistance=10k package=THT]
  Part1 = Arduino Nano (Rev3.0)
  JACK2 = 2.1mm Barrel Jack with Terminal Block
  Part16 = RFID-RC522-v3
  Part17 = RFID-RC522-v3
  Part18 = RFID-RC522-v3
  Part19 = Arduino Nano (Rev3.0)
  Part20 = RFID-RC522-v3
  Part21 = RFID-RC522-v3
  Part22 = RFID-RC522-v3
  Part23 = Arduino Nano (Rev3.0)

nets:
  N1: Part2.SDA, Part1.D3
  N2: Part2.SCK, Part3.SCK, Part5.SCK, Part1.D13/SCK
  N3: Part2.MOSI, Part3.MOSI, Part5.MOSI, Part1.D11/MOSI
  N4: Part2.MISO, Part3.MISO, Part5.MISO, Part1.D12/MISO
  GND: Part2.GND, Part3.GND, Part5.GND, Part1.GND, JACK2.NEG, Part16.GND, Part17.GND, Part18.GND, Part19.GND, Part20.GND, Part21.GND, Part22.GND, Part23.GND
  N5: Part2.RST, Part3.RST, Part5.RST, Part1.D8
  3.3V: Part2.3.3V, Part3.3.3V, Part5.3.3V, JACK2.POS, Part16.3.3V, Part17.3.3V, Part18.3.3V, Part20.3.3V, Part21.3.3V, Part22.3.3V
  N6: Part3.SDA, Part1.D2
  N7: KY-1.signal, Part15.D7
  N8: KY-1.power, Part15.5V, R1.Pin_1, R2.Pin_1
  N9: KY-1.ground, Part15.GND
  N10: KY-1.C, JACK1.POS
  N11: KY-1.NO, L1.pin2
  N12: JACK1.NEG, L1.pin1
  N13: Part5.SDA, Part1.D4
  N14: Part15.A4/SDA, R1.Pin_0, Part1.A4, Part19.A4, Part23.A4
  N15: Part15.A5/SCL, R2.Pin_0, Part1.A5, Part19.A5, Part23.A5
  N16: Part16.SDA, Part19.D2
  N17: Part16.SCK, Part17.SCK, Part18.SCK, Part19.D13/SCK
  N18: Part16.MOSI, Part17.MOSI, Part18.MOSI, Part19.D11/MOSI
  N19: Part16.MISO, Part17.MISO, Part18.MISO, Part19.D12/MISO
  N20: Part16.RST, Part17.RST, Part18.RST, Part19.D8
  N21: Part17.SDA, Part19.D4
  N22: Part18.SDA, Part19.D3
  N23: Part20.SDA, Part23.D2
  N24: Part20.SCK, Part21.SCK, Part22.SCK, Part23.D13/SCK
  N25: Part20.MOSI, Part21.MOSI, Part22.MOSI, Part23.D11/MOSI
  N26: Part20.MISO, Part21.MISO, Part22.MISO, Part23.D12/MISO
  N27: Part20.RST, Part21.RST, Part22.RST, Part23.D8
  N28: Part21.SDA, Part23.D4
  N29: Part22.SDA, Part23.D3

notes:
  Every RFID sensor is connected to the SPI pins of the corresponding slave Arduino (see https://www.arduino.cc/en/Reference/SPI).
  Sensors also share a common reset pin, although they each have a unique Slave Select pin assigned to them.
  They are powered by a separate +3.3V DC input, with a common ground shared to the Arduino
  SDA/SS (Slave Select) : Pin 2/3/4. Unique for each reader and defined in code
  SCK (System Clock) : Pin 13
  MOSI (Master Out, Slave In) : Pin 11
  MISO (Master In, Slave Out) : Pin 12
  GND (Ground) : -ve DC/ Arduino Ground
  RST (Reset) : Pin 8
  3.3V (Power) : +ve DC
  3.3VDC Power Supply
  to RFID readers
  Slave A
  Slave B
  Slave C
  Master
  I2C drivers use an "open drain" system. That is to say, the signal lines are normally HIGH, and devices pull it LOW when communicating.
  10kΩ resistors placed between both I2C lines and 5V to pull the signal up.

custom parts:
  RFID-RC522-v3: A simple China made RFID-RC522 Reader (6x4 cm); do check the pin labels, as this is a MFRC522 based clone.
  Keyes Relay: The Keyes 5V relay module is suitable for SCM development, home appliance control. It uses a 5V~12V TIL control signal which can control DC / AC signal.
